# Fritzing sketch pcb2 (saved by Fritzing 0.9.3b)
perfboards: 1

parts:
  J1 = female pin header, 16 pins [form="♀ (female)"]
  R1 = Trimmer Potentiometer [maximum_resistance=10kΩ package=THT]
  R2 = Resistor [tolerance=±5% resistance=220 package="2512 [SMD]"]
  J3 = male pin header, 6 pins [form="♂ (male)"]
  J4 = male pin header, 2 pins [form="♂ (male)"]
  J5 = male pin header, 1 pin [form="♂ (male)"]
  J7 = male pin header, 1 pin [form="♂ (male)"]  # not connected

nets:
  N1: J1.pin1, J5.pin1
  N2: J1.pin2, R2.Pin_0
  N3: J1.pin3, J3.pin1
  N4: J1.pin4, J3.pin2
  N5: J1.pin5, J3.pin3
  N6: J1.pin6, J3.pin4
  N7: J1.pin11, J3.pin5
  N8: J1.pin13, J3.pin6
  N9: J1.pin14, R1.wiper
  N10: J1.pin15, J4.pin1
  N11: J1.pin16, J4.pin2
  N12: R1.leg2, R2.Pin_1
